// Logisim project Diagramas.circ as structural Verilog: 9 circuits, main circuit main
module main (
  input  [2:0] in_1,
  output [7:0] out_2
);

  \Critério_Custo_por_Entrada_7  CCE7_C___24 (.E0(in_1[2]), .E1(in_1[1]), .E2(in_1[0]), .S(out_2[0]));
  Criterio_Custo_Por_Entrada_3 CCE3_C___46 (.E0(in_1[2]), .E1(in_1[1]), .E2(in_1[0]), .S(out_2[1]));
  \Critério_Custo_Por_Entrada_1  CCE1_C_26 (.E0(in_1[2]), .E1(in_1[1]), .E2(in_1[0]), .S(out_2[3]));
  \Critério_Custo_Por_Entrada_2  CCE2_C___16 (.E0(in_1[2]), .E1(in_1[1]), .E2(in_1[0]), .S(out_2[2]));
  \Critério_Custo_Por_Entrada_Fixo_2  CCEF2_C_34 (.E0(in_1[2]), .E1(in_1[1]), .E2(in_1[0]), .S(out_2[4]));
  \Critério_Custo_Por_Entrada_Fixo_1  CCEF1_C___24 (.E0(in_1[2]), .E1(in_1[1]), .E2(in_1[0]), .S(out_2[5]));
  CriterioPortas CQtdPortas_C_38 (.E0(in_1[2]), .E1(in_1[1]), .E2(in_1[0]), .S(out_2[6]));
  Karnaugh Karnaugh_C_33 (.E0(in_1[2]), .E1(in_1[1]), .E2(in_1[0]), .S(out_2[7]));
endmodule

module Karnaugh (
  input  E0,
  input  E1,
  input  E2,
  output S
);

  wire and_1_out, and_2_out, and_3_out, not_1_out, not_2_out;

  not not_1 (not_1_out, E0);
  not not_2 (not_2_out, E1);
  and and_1 (and_1_out, not_1_out, E1);
  and and_2 (and_2_out, not_1_out, E2);
  and and_3 (and_3_out, not_2_out, E2);
  or or_1 (S, and_1_out, and_2_out, and_3_out);
endmodule

module CriterioPortas (
  input  E0,
  input  E1,
  input  E2,
  output S
);

  wire and_1_out, not_1_out, not_2_out, xnor_1_out, xor_1_out;

  not not_1 (not_1_out, E1);
  xnor xnor_1 (xnor_1_out, E2, not_1_out);
  xor xor_1 (xor_1_out, xnor_1_out, E0);
  not not_2 (not_2_out, E2);
  and and_1 (and_1_out, xor_1_out, E1);
  xnor xnor_2 (S, and_1_out, not_2_out);
endmodule

module \Critério_Custo_Por_Entrada_Fixo_1  (
  input  E0,
  input  E1,
  input  E2,
  output S
);

  wire and_1_out, xnor_1_out;

  xnor xnor_1 (xnor_1_out, E0, E2);
  and and_1 (and_1_out, xnor_1_out, E1);
  xor xor_1 (S, and_1_out, E2);
endmodule

module \Critério_Custo_Por_Entrada_Fixo_2  (
  input  E0,
  input  E1,
  input  E2,
  output S
);

  wire and_1_out, nor_1_out, nor_2_out, not_1_out, xor_1_out;

  not not_1 (not_1_out, E0);
  nor nor_1 (nor_1_out, not_1_out, 1'b0);
  and and_1 (and_1_out, nor_1_out, 1'b1);
  xor xor_1 (xor_1_out, and_1_out, E2);
  nor nor_2 (nor_2_out, xor_1_out, E1);
  xnor xnor_1 (S, nor_2_out, E0);
endmodule

module \Critério_Custo_Por_Entrada_1  (
  input  E0,
  input  E1,
  input  E2,
  output S
);

  wire nand_1_out, not_1_out, or_1_out, xor_1_out;

  not not_1 (not_1_out, E1);
  xor xor_1 (xor_1_out, not_1_out, 1'b1);
  nand nand_1 (nand_1_out, xor_1_out, E0);
  or or_1 (or_1_out, E1, E2);
  and and_1 (S, nand_1_out, or_1_out);
endmodule

module \Critério_Custo_Por_Entrada_2  (
  input  E0,
  input  E1,
  input  E2,
  output S
);

  wire nand_1_out, or_1_out;

  nand nand_1 (nand_1_out, E0, E1);
  or or_1 (or_1_out, E1, E2);
  and and_1 (S, nand_1_out, or_1_out);
endmodule

module Criterio_Custo_Por_Entrada_3 (
  input  E0,
  input  E1,
  input  E2,
  output S
);

  wire and_1_out, nor_1_out, nor_2_out, not_1_out, or_1_out, xnor_1_out, xor_1_out;

  xnor xnor_1 (xnor_1_out, E1, 1'b1);
  and and_1 (and_1_out, 1'b1, E2);
  nor nor_1 (nor_1_out, E1, E0);
  or or_1 (or_1_out, xnor_1_out, and_1_out);
  nor nor_2 (nor_2_out, nor_1_out, E0);
  not not_1 (not_1_out, E1);
  xor xor_1 (xor_1_out, nor_2_out, not_1_out);
  and and_2 (S, or_1_out, xor_1_out);
endmodule

module \Critério_Custo_por_Entrada_7  (
  input  E0,
  input  E1,
  input  E2,
  output S
);

  wire and_1_out, nand_1_out, nor_1_out, not_1_out;

  nand nand_1 (nand_1_out, 1'b1, E1);
  not not_1 (not_1_out, E1);
  nor nor_1 (nor_1_out, E0, nand_1_out);
  and and_1 (and_1_out, E2, not_1_out);
  xor xor_1 (S, nor_1_out, and_1_out);
endmodule
