// Logisim project 01.circ as structural Verilog: 1 circuit, main circuit main
module main (
  input  E0,
  input  E1,
  input  E2,
  output out_4,
  output out_5
);

  wire and_1_out, and_2_out, nand_1_out, not_1_out, not_2_out, or_1_out;

  not not_1 (not_1_out, E0);
  not not_2 (not_2_out, E1);
  and and_1 (and_1_out, E1, not_1_out);
  and and_2 (and_2_out, E2, not_2_out);
  nand nand_1 (nand_1_out, E1, E0);
  or or_1 (or_1_out, E2, E1);
  or or_2 (out_4, and_1_out, and_2_out);
  and and_3 (out_5, nand_1_out, or_1_out);

  // Notes on the sheet:
  //   T 01 - C 22
  //   T 04 - C 16
endmodule
