// Logisim project 02.circ as structural Verilog: 1 circuit, main circuit main
module main (
  input  E0,
  input  E1,
  input  E2,
  input  E3,
  output out_5,
  output out_6
);

  wire and_1_out, and_2_out, and_3_out, and_4_out, and_5_out, and_6_out, and_7_out, nor_1_out, not_1_out,
       not_2_out, not_3_out, not_4_out, not_5_out, not_6_out, not_7_out, not_8_out;

  not not_1 (not_1_out, E2);
  not not_2 (not_2_out, E0);
  not not_3 (not_3_out, E3);
  not not_4 (not_4_out, E3);
  not not_5 (not_5_out, E0);
  not not_6 (not_6_out, E2);
  not not_7 (not_7_out, E0);
  not not_8 (not_8_out, E3);
  and and_1 (and_1_out, not_1_out, E1, not_2_out);
  and and_2 (and_2_out, not_3_out, E1);
  and and_3 (and_3_out, not_4_out, not_5_out);
  and and_4 (and_4_out, E3, E2, E0);
  and and_5 (and_5_out, E3, E2, E0);
  nor nor_1 (nor_1_out, E3, E0);
  and and_6 (and_6_out, not_8_out, E1);
  and and_7 (and_7_out, not_6_out, E1, not_7_out);
  or or_1 (out_5, and_1_out, and_2_out, and_3_out, and_4_out);
  or or_2 (out_6, and_5_out, nor_1_out, and_6_out, and_7_out);

  // Notes on the sheet:
  //   C 48
endmodule
